# Fritzing sketch OpenLung_ArduinoShield_LCD_BLUETOOTH (saved by Fritzing 0.9.3b)
circuit board: 8.53339cm x 6.07816cm
breadboards: 1

parts:
  Componente1 = Arduino Uno (Rev3)
  Pololu_A1 = Pololu A4988 [package=SO16]
  J1 = Power Jack [package=power_jack_pth_lock]
  M1 = BME280
  J2 = female pin header, 4 pins [form="♀ (female)"]
  LED1 = LED - 5mm [color="Red (633nm)" package="5 mm [THT]"]
  R1 = Resistor [tolerance=±5% resistance=220 package=THT]
  R2 = Rotary Potentiometer (Large) [maximum_resistance=10kΩ package=THT]
  U1 = LCD-16X2 [package=lcd-16x2]
  R3 = TRIMPOT [package=trim_pot_pth]
  SG1 = Buzzer 12mm [package=buzzer-12mm]  # not connected
  S1 = Pushbutton [package="[THT]"]
  R4 = Resistor [tolerance=±5% resistance=220 package=THT]
  SG2 = Buzzer 12mm [package=buzzer-12mm-ns-kit]
  Part2 = Bluetooth HC-05 Macho

nets:
  N1: Componente1.A0, R2.wiper
  N2: Componente1.A4/SDA, M1.SDA
  N3: Componente1.A5/SCL, M1.SCL
  N4: Componente1.D8, U1.DB7
  N5: Componente1.D9_PWM, U1.DB6
  N6: Componente1.D10_PWM/SS, U1.DB5
  N7: Componente1.D11_PWM/MOSI, U1.DB4
  N8: Componente1.D12/MISO, SG2.1
  N9: Componente1.D13/SCK, R1.Pin_1
  GND: Componente1.GND, Pololu_A1.GND#8, M1.GND, LED1.cathode, R2.leg1, U1.VSS, U1.R_W, R3.CW, R4.Pin_0, SG2.2
  N10: Componente1.D0/RX, Part2.TXD
  N11: Componente1.D1/TX, Part2.RXD
  N12: Componente1.D2, Pololu_A1.ENABLE
  N13: Componente1.D3_PWM, Pololu_A1.DIR
  N14: Componente1.D4, Pololu_A1.STEP
  N15: Componente1.D5_PWM, U1.RS
  N16: Componente1.D6_PWM, S1.Pin_1, S1.Pin_2, R4.Pin_1
  N17: Componente1.D7, U1.E
  3V3: Componente1.3V3, M1.VIN
  VDD: Componente1.5V, Pololu_A1.RESET, Pololu_A1.SLEEP, Pololu_A1.VDD, R2.leg2, U1.VDD, R3.CCW, S1.Pin_3, S1.Pin_4, Part2.VCC
  N18: Componente1.VIN, Pololu_A1.VMOT, J1.PWR
  N19: Pololu_A1.1B, J2.pin4
  N20: Pololu_A1.1A, J2.pin3
  N21: Pololu_A1.2A, J2.pin2
  N22: Pololu_A1.2B, J2.pin1
  GND_2: Pololu_A1.GND#14, J1.GND, Part2.GND
  N23: LED1.anode, R1.Pin_0
  N24: U1.VO, R3.WIPER

custom parts:
  BME280: Temperature Humidity Barometric presure Sensor
